# Fritzing sketch green-house-sketch (saved by Fritzing 0.9.3b)

parts:
  Raspberry_Pi_1 = Raspberry Pi 3 [part_number=RPI-3-V1.2]
  Реле = 2-Channel 5v Relay Shield [package=relay-2ch5v10a]
  Датчик_влажности/температуры = HTU21D-F Temperature + Humidity Sensor

nets:
  3V3: Raspberry_Pi_1.3v3, Датчик_влажности/температуры.VIN, Датчик_влажности/температуры.+3V3
  N1: Raspberry_Pi_1.GPIO2, Датчик_влажности/температуры.SDA
  N2: Raspberry_Pi_1.GPIO3, Датчик_влажности/температуры.SCL
  GND: Raspberry_Pi_1.GND, Реле.GND, Датчик_влажности/температуры.GND
  N3: Raspberry_Pi_1.GPIO21, Реле.IN1
  N4: Raspberry_Pi_1.GPIO20, Реле.IN2
  5V: Raspberry_Pi_1.5V, Реле.VCC

notes:
  Для выхода на реле
  Красный: 12V
  Черный: земля
  Желтый: на освещение
  (второй контакт освещения на землю)
  Оранжевый: на полив
  (второй контакт полива на землю)

custom parts:
  2-Channel 5v Relay Shield: 2 Channel 5v Relay Shield w. 2x SPD-06VDC-SD-C
  HTU21D-F Temperature + Humidity Sensor: This I2C digital humidity sensor is an accurate and intelligent alternative to the much simpler Humidity and Temperature Sensor - SHT15 Breakout It has a typical accuracy of ±2% with an operating range that's optimized from 5% to 95% RH. Operation outside this range is still possible - just the accuracy might drop a bit. The temperature output has an accuracy of ±1°C from -30~90°C. If you're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
